// Logisim project cpu.circ as structural Verilog: 1 circuit, main circuit main
module main (
  input  [31:0] INSTRUCTION,
  input  CLOCK,
  output [31:0] FETCH_ADDRESS,
  output [31:0] s0_Value,
  output [31:0] s1_Value,
  output [31:0] s2_Value,
  output [31:0] ra_Value,
  output [31:0] sp_Value
);

  wire add, addi, addiu, addu, ALUSrc, \and , and_1_out, and_2_out, and_3_out, andi, beq, bne, Branch,
       comparator_27_eq, comparator_28_eq, comparator_29_eq, comparator_31_eq, comparator_32_eq,
       comparator_33_eq, comparator_34_eq, comparator_35_eq, comparator_36_eq, comparator_37_eq,
       comparator_38_eq, comparator_39_eq, comparator_40_eq, comparator_41_eq, comparator_42_eq,
       comparator_43_eq, comparator_44_eq, comparator_45_eq, comparator_46_eq, comparator_47_eq,
       comparator_48_eq, comparator_49_eq, comparator_50_eq, comparator_51_eq, comparator_52_eq,
       comparator_53_eq, comparator_54_eq, comparator_55_eq, comparator_57_eq, comparator_58_eq,
       comparator_59_eq, comparator_60_eq, comparator_61_eq, ExtOp, j, jal, jr, Jump, lui, lw, main_2_equal,
       main_2_signed_overflow, MemToReg, MemWr, Nop, not_1_out, not_2_out, not_3_out, not_4_out, not_5_out,
       not_6_out, \or , or_7_out, or_8_out, or_11_out, or_12_out, or_13_out, or_14_out, ori, RegDst, RegWr,
       Shift, sll, slt, slti, sltiu, sltu, sra, srl, sub, subu, sw, swinc;
  wire [3:0] adder_2_out_2, ALUCtr, multiplexer_4_out, multiplexer_6_out, multiplexer_7_out,
       multiplexer_8_out, multiplexer_9_out, multiplexer_11_out, multiplexer_14_out, multiplexer_15_out,
       multiplexer_16_out, multiplexer_18_out;
  wire [4:0] multiplexer_3_out;
  wire [5:0] funct;
  wire [25:0] shifter_1_out;
  wire [27:0] adder_2_out;
  wire [31:0] adder_1_out, adder_3_out, bit_extender_1_out, bit_extender_2_out, bit_extender_3_out,
       bit_extender_4_out, main_1_read_data_1, main_1_read_data_2, main_2_result, main_3_p5,
       multiplexer_1_out, multiplexer_2_out, multiplexer_5_out, multiplexer_10_out, multiplexer_12_out,
       multiplexer_13_out, multiplexer_17_out, multiplexer_20_out, multiplexer_21_out, shifter_2_out;
  wire [31:6] instruction_t;

  Adder #(.width(32)) adder_1 (
    .a({adder_2_out_2, {28{1'b0}}}), .b(bit_extender_2_out), .out(adder_1_out));  // open: cin, cout
  Multiplexer #(.width(32)) multiplexer_1 (
    .in0(multiplexer_17_out), .in1(adder_1_out), .out(multiplexer_1_out), .sel(Jump));  // open: en
  Register #(.width(32)) PC (.D(multiplexer_1_out), .Q(FETCH_ADDRESS), .clk(CLOCK));  // open: en, clr
  Comparator #(.width(6)) comparator_1 (.a(funct), .b(6'b100000), .eq(add));  // open: gt, lt
  Comparator #(.width(6)) comparator_2 (.a(instruction_t[31:26]), .b(6'b001000), .eq(addi));  // open: gt, lt
  Comparator #(.width(6)) comparator_3 (.a(instruction_t[31:26]), .b(6'b001001), .eq(addiu));  // open: gt, lt
  Comparator #(.width(6)) comparator_4 (.a(funct), .b(6'b100001), .eq(addu));  // open: gt, lt
  Comparator #(.width(6)) comparator_5 (.a(funct), .b(6'b100100), .eq(\and ));  // open: gt, lt
  Comparator #(.width(6)) comparator_6 (.a(instruction_t[31:26]), .b(6'b001100), .eq(andi));  // open: gt, lt
  Comparator #(.width(6)) comparator_7 (.a(instruction_t[31:26]), .b(6'b000100), .eq(beq));  // open: gt, lt
  Comparator #(.width(6)) comparator_8 (.a(instruction_t[31:26]), .b(6'b000101), .eq(bne));  // open: gt, lt
  Comparator #(.width(6)) comparator_9 (.a(instruction_t[31:26]), .b(6'b000010), .eq(j));  // open: gt, lt
  Comparator #(.width(6)) comparator_10 (.a(instruction_t[31:26]), .b(6'b000011), .eq(jal));  // open: gt, lt
  Comparator #(.width(6)) comparator_11 (.a(funct), .b(6'b001000), .eq(jr));  // open: gt, lt
  Comparator #(.width(6)) comparator_12 (.a(instruction_t[31:26]), .b(6'b001111), .eq(lui));  // open: gt, lt
  Comparator #(.width(6)) comparator_13 (.a(instruction_t[31:26]), .b(6'b100011), .eq(lw));  // open: gt, lt
  Comparator #(.width(6)) comparator_14 (.a(funct), .b(6'b100101), .eq(\or ));  // open: gt, lt
  Comparator #(.width(6)) comparator_15 (.a(instruction_t[31:26]), .b(6'b001101), .eq(ori));  // open: gt, lt
  Comparator #(.width(6)) comparator_16 (.a(funct), .b(6'b101010), .eq(slt));  // open: gt, lt
  Comparator #(.width(6)) comparator_17 (.a(instruction_t[31:26]), .b(6'b001010), .eq(slti));  // open: gt, lt
  Comparator #(.width(6)) comparator_18 (.a(instruction_t[31:26]), .b(6'b001011), .eq(sltiu));  // open: gt, lt
  Comparator #(.width(6)) comparator_19 (.a(funct), .b(6'b101011), .eq(sltu));  // open: gt, lt
  Comparator #(.width(6)) comparator_20 (.a(funct), .b({6{1'b0}}), .eq(sll));  // open: gt, lt
  Comparator #(.width(6)) comparator_21 (.a(funct), .b(6'b000011), .eq(sra));  // open: gt, lt
  Comparator #(.width(6)) comparator_22 (.a(funct), .b(6'b000010), .eq(srl));  // open: gt, lt
  Comparator #(.width(6)) comparator_23 (.a(instruction_t[31:26]), .b(6'b101011), .eq(sw));  // open: gt, lt
  Comparator #(.width(6)) comparator_24 (.a(instruction_t[31:26]), .b(6'b101100), .eq(swinc));  // open: gt, lt
  Comparator #(.width(6)) comparator_25 (.a(funct), .b(6'b100010), .eq(sub));  // open: gt, lt
  Comparator #(.width(6)) comparator_26 (.a(funct), .b(6'b100011), .eq(subu));  // open: gt, lt
  Adder #(.width(32)) adder_2 (.a(FETCH_ADDRESS), .b(32'h4), .out({adder_2_out_2, adder_2_out}));  // open: cin, cout
  Comparator #(.width(6)) comparator_27 (
    .a(instruction_t[31:26]), .b(6'b000010), .eq(comparator_27_eq));  // open: gt, lt
  Comparator #(.width(6)) comparator_28 (
    .a(instruction_t[31:26]), .b(6'b000011), .eq(comparator_28_eq));  // open: gt, lt
  Comparator #(.width(6)) comparator_29 (.a(funct), .b(6'b001000), .eq(comparator_29_eq));  // open: gt, lt
  and and_1 (and_1_out, comparator_29_eq, RegDst);
  Comparator #(.width(6)) comparator_30 (.a(instruction_t[31:26]), .b({6{1'b0}}), .eq(RegDst));  // open: gt, lt
  Comparator #(.width(6)) comparator_31 (
    .a(instruction_t[31:26]), .b(6'b001000), .eq(comparator_31_eq));  // open: gt, lt
  Comparator #(.width(6)) comparator_32 (
    .a(instruction_t[31:26]), .b(6'b001001), .eq(comparator_32_eq));  // open: gt, lt
  Comparator #(.width(6)) comparator_33 (
    .a(instruction_t[31:26]), .b(6'b001111), .eq(comparator_33_eq));  // open: gt, lt
  Comparator #(.width(6)) comparator_34 (
    .a(instruction_t[31:26]), .b(6'b100011), .eq(comparator_34_eq));  // open: gt, lt
  Comparator #(.width(6)) comparator_35 (
    .a(instruction_t[31:26]), .b(6'b001010), .eq(comparator_35_eq));  // open: gt, lt
  Comparator #(.width(6)) comparator_36 (
    .a(instruction_t[31:26]), .b(6'b001011), .eq(comparator_36_eq));  // open: gt, lt
  Comparator #(.width(6)) comparator_37 (
    .a(instruction_t[31:26]), .b(6'b101011), .eq(comparator_37_eq));  // open: gt, lt
  Comparator #(.width(6)) comparator_38 (
    .a(instruction_t[31:26]), .b(6'b101100), .eq(comparator_38_eq));  // open: gt, lt
  not not_1 (not_1_out, comparator_39_eq);
  Comparator #(.width(6)) comparator_39 (
    .a(instruction_t[31:26]), .b(6'b000100), .eq(comparator_39_eq));  // open: gt, lt
  not not_2 (not_2_out, comparator_40_eq);
  Comparator #(.width(6)) comparator_40 (
    .a(instruction_t[31:26]), .b(6'b000101), .eq(comparator_40_eq));  // open: gt, lt
  Comparator #(.width(6)) comparator_41 (
    .a(instruction_t[31:26]), .b(6'b000010), .eq(comparator_41_eq));  // open: gt, lt
  not not_3 (not_3_out, comparator_41_eq);
  Comparator #(.width(6)) comparator_42 (
    .a(instruction_t[31:26]), .b(6'b001000), .eq(comparator_42_eq));  // open: gt, lt
  not not_4 (not_4_out, comparator_42_eq);
  Comparator #(.width(6)) comparator_43 (
    .a(instruction_t[31:26]), .b(6'b101011), .eq(comparator_43_eq));  // open: gt, lt
  not not_5 (not_5_out, comparator_43_eq);
  Comparator #(.width(6)) comparator_44 (
    .a(instruction_t[31:26]), .b(6'b001000), .eq(comparator_44_eq));  // open: gt, lt
  Comparator #(.width(6)) comparator_45 (
    .a(instruction_t[31:26]), .b(6'b001001), .eq(comparator_45_eq));  // open: gt, lt
  Comparator #(.width(6)) comparator_46 (
    .a(instruction_t[31:26]), .b(6'b001100), .eq(comparator_46_eq));  // open: gt, lt
  Comparator #(.width(6)) comparator_47 (
    .a(instruction_t[31:26]), .b(6'b001111), .eq(comparator_47_eq));  // open: gt, lt
  Comparator #(.width(6)) comparator_48 (
    .a(instruction_t[31:26]), .b(6'b100011), .eq(comparator_48_eq));  // open: gt, lt
  Comparator #(.width(6)) comparator_49 (
    .a(instruction_t[31:26]), .b(6'b001101), .eq(comparator_49_eq));  // open: gt, lt
  Comparator #(.width(6)) comparator_50 (
    .a(instruction_t[31:26]), .b(6'b001010), .eq(comparator_50_eq));  // open: gt, lt
  Comparator #(.width(6)) comparator_51 (
    .a(instruction_t[31:26]), .b(6'b001011), .eq(comparator_51_eq));  // open: gt, lt
  Comparator #(.width(6)) comparator_52 (
    .a(instruction_t[31:26]), .b(6'b101011), .eq(comparator_52_eq));  // open: gt, lt
  Comparator #(.width(6)) comparator_53 (
    .a(instruction_t[31:26]), .b(6'b101100), .eq(comparator_53_eq));  // open: gt, lt
  Comparator #(.width(6)) comparator_54 (
    .a(instruction_t[31:26]), .b(6'b101011), .eq(comparator_54_eq));  // open: gt, lt
  or or_1 (MemWr, comparator_54_eq, comparator_55_eq);
  Comparator #(.width(6)) comparator_55 (
    .a(instruction_t[31:26]), .b(6'b101100), .eq(comparator_55_eq));  // open: gt, lt
  Comparator #(.width(6)) comparator_56 (.a(instruction_t[31:26]), .b(6'b100011), .eq(MemToReg));  // open: gt, lt
  Comparator #(.width(6)) comparator_57 (
    .a(instruction_t[31:26]), .b(6'b000100), .eq(comparator_57_eq));  // open: gt, lt
  Comparator #(.width(6)) comparator_58 (
    .a(instruction_t[31:26]), .b(6'b000101), .eq(comparator_58_eq));  // open: gt, lt
  Shifter #(.width(26)) shifter_1 (.in({instruction_t[25:6], funct}), .\dist (5'b00010), .out(shifter_1_out));
  assign bit_extender_1_out = {{26{1'b0}}, instruction_t[11:6]};  // Bit_Extender bit_extender_1
  or or_2 (Jump, comparator_27_eq, comparator_28_eq, and_1_out);
  or or_3 (ExtOp, comparator_31_eq, comparator_32_eq, comparator_33_eq, comparator_34_eq, comparator_35_eq, comparator_36_eq, comparator_37_eq, comparator_38_eq);
  or or_4 (RegWr, not_1_out, not_2_out, not_3_out, not_4_out, not_5_out);
  or or_5 (ALUSrc, comparator_44_eq, comparator_45_eq, comparator_46_eq, comparator_47_eq, comparator_48_eq, comparator_49_eq, comparator_50_eq, comparator_51_eq, comparator_52_eq, comparator_53_eq);
  or or_6 (Branch, comparator_57_eq, comparator_58_eq);
  Multiplexer #(.width(32)) multiplexer_2 (
    .in0(INSTRUCTION), .in1({32{1'b0}}), .out(multiplexer_2_out), .sel(Nop));  // open: en
  Register #(.width(32)) register_1 (.D(multiplexer_2_out), .Q({instruction_t, funct}), .clk(CLOCK));  // open: en, clr
  assign bit_extender_2_out = {{6{1'b0}}, shifter_1_out};  // Bit_Extender bit_extender_2
  Multiplexer #(.width(5)) multiplexer_3 (
    .in0(instruction_t[20:16]), .in1(instruction_t[15:11]), .out(multiplexer_3_out), .sel(RegDst));  // open: en
  Multiplexer #(.width(4)) multiplexer_4 (
    .in0(4'b0000), .in1(4'b0000), .out(multiplexer_4_out), .sel(sll));  // open: en
  assign bit_extender_3_out = {{16{instruction_t[15]}}, {instruction_t[15:6], funct}};  // Bit_Extender bit_extender_3
  Multiplexer #(.width(32)) multiplexer_5 (
    .in0(bit_extender_3_out), .in1(bit_extender_4_out), .out(multiplexer_5_out), .sel(ExtOp));  // open: en
  assign bit_extender_4_out = {{16{1'b0}}, {instruction_t[15:6], funct}};  // Bit_Extender bit_extender_4
  Multiplexer #(.width(4)) multiplexer_6 (
    .in0(multiplexer_4_out), .in1(4'b0001), .out(multiplexer_6_out), .sel(srl));  // open: en
  Multiplexer #(.width(4)) multiplexer_7 (
    .in0(multiplexer_6_out), .in1(4'b0010), .out(multiplexer_7_out), .sel(sra));  // open: en
  Multiplexer #(.width(4)) multiplexer_8 (
    .in0(multiplexer_7_out), .in1(4'b0101), .out(multiplexer_8_out), .sel(or_7_out));  // open: en
  or or_7 (or_7_out, add, addi);
  Comparator #(.width(6)) comparator_59 (.a(funct), .b({6{1'b0}}), .eq(comparator_59_eq));  // open: gt, lt
  Comparator #(.width(6)) comparator_60 (.a(funct), .b(6'b000011), .eq(comparator_60_eq));  // open: gt, lt
  Comparator #(.width(6)) comparator_61 (.a(funct), .b(6'b000010), .eq(comparator_61_eq));  // open: gt, lt
  regfile_main main_1 (
    .Read_Register_1(instruction_t[25:21]), .Read_Register_2(instruction_t[20:16]),
    .Write_Register(multiplexer_3_out), .Write_Data(multiplexer_21_out), .Write_Enable(RegWr), .Clock(CLOCK),
    .Read_Data_1(main_1_read_data_1), .Read_Data_2(main_1_read_data_2), .s0_Value(s0_Value),
    .s1_Value(s1_Value), .s2_Value(s2_Value), .ra_Value(ra_Value), .sp_Value(sp_Value));
  Multiplexer #(.width(4)) multiplexer_9 (
    .in0(multiplexer_8_out), .in1(4'b0110), .out(multiplexer_9_out), .sel(or_8_out));  // open: en
  or or_8 (or_8_out, addu, addiu);
  or or_9 (Shift, comparator_59_eq, comparator_60_eq, comparator_61_eq);
  or or_10 (Nop, Jump, Branch);
  Shifter #(.width(32)) shifter_2 (.in(multiplexer_5_out), .\dist (5'b00010), .out(shifter_2_out));
  Multiplexer #(.width(32)) multiplexer_10 (
    .in0(main_1_read_data_2), .in1(multiplexer_5_out), .out(multiplexer_10_out), .sel(ALUSrc));  // open: en
  Multiplexer #(.width(4)) multiplexer_11 (
    .in0(multiplexer_9_out), .in1(4'b0111), .out(multiplexer_11_out), .sel(sub));  // open: en
  Adder #(.width(32)) adder_3 (
    .a({adder_2_out_2, adder_2_out}), .b(multiplexer_20_out), .out(adder_3_out));  // open: cin, cout
  Multiplexer #(.width(32)) multiplexer_12 (
    .in0(multiplexer_13_out), .in1(32'h10), .out(multiplexer_12_out), .sel(lui));  // open: en
  Multiplexer #(.width(32)) multiplexer_13 (
    .in0(main_1_read_data_1), .in1(bit_extender_1_out), .out(multiplexer_13_out), .sel(Shift));  // open: en
  Multiplexer #(.width(4)) multiplexer_14 (
    .in0(multiplexer_11_out), .in1(4'b1000), .out(multiplexer_14_out), .sel(subu));  // open: en
  Multiplexer #(.width(4)) multiplexer_15 (
    .in0(multiplexer_14_out), .in1(4'b1001), .out(multiplexer_15_out), .sel(or_11_out));  // open: en
  or or_11 (or_11_out, \and , andi);
  LED led_1 (.in(main_2_signed_overflow));
  alu_main main_2 (
    .Switch(ALUCtr), .X(multiplexer_12_out), .Equal(main_2_equal), .Result(main_2_result),
    .Signed_Overflow(main_2_signed_overflow), .Y(multiplexer_10_out));
  Multiplexer #(.width(4)) multiplexer_16 (
    .in0(multiplexer_15_out), .in1(4'b1010), .out(multiplexer_16_out), .sel(or_12_out));  // open: en
  or or_12 (or_12_out, \or , ori);
  Multiplexer #(.width(32)) multiplexer_17 (
    .in0({adder_2_out_2, adder_2_out}), .in1(adder_3_out), .out(multiplexer_17_out), .sel(Branch));  // open: en
  Multiplexer #(.width(4)) multiplexer_18 (
    .in0(multiplexer_16_out), .in1(4'b1011), .out(multiplexer_18_out), .sel(or_13_out));  // open: en
  or or_13 (or_13_out, slt, slti);
  or or_14 (or_14_out, sltu, sltiu);
  Multiplexer #(.width(4)) multiplexer_19 (
    .in0(multiplexer_18_out), .in1(4'b1100), .out(ALUCtr), .sel(or_14_out));  // open: en
  Multiplexer #(.width(32)) multiplexer_20 (
    .in0({32{1'b0}}), .in1(shifter_2_out), .out(multiplexer_20_out), .sel(Branch));  // open: en
  or or_15 (Branch, and_2_out, and_3_out);
  and and_2 (and_2_out, main_2_equal, beq);
  and and_3 (and_3_out, not_6_out, bne);
  not not_6 (not_6_out, main_2_equal);
  // mem_main main_3: pin names not known; wires that end beside it: main_2_result, main_1_read_data_2, MemWr, CLOCK, main_3_p5
  Multiplexer #(.width(32)) multiplexer_21 (
    .in0(main_2_result), .in1(main_3_p5), .out(multiplexer_21_out), .sel(MemToReg));  // open: en

  // Other names for the same wires on the sheet: clk = CLOCK; fetch_addr[31:0] = FETCH_ADDRESS;
  //   instruction_t[5:0] = funct; opcode[5:0] = instruction_t[31:26]; ra[31:0] = ra_Value; s0[31:0] = s0_Value;
  //   s1[31:0] = s1_Value; s2[31:0] = s2_Value; sp[31:0] = sp_Value; SuccessBranch = Branch

  // Notes on the sheet:
  //   Output
  //   These are outputs/inputs from run.circ
  //   Inputs
  //   These are DEBUG/TEST outputs from your circuit.
endmodule
