// Logisim project regfile.circ as structural Verilog: 1 circuit, main circuit main
module main (
  input  [4:0] Read_Register_1,
  input  [4:0] Read_Register_2,
  input  [4:0] Write_Register,
  input  [31:0] Write_Data,
  input  Write_Enable,
  input  Clock,
  output [31:0] s0_Value,
  output [31:0] s1_Value,
  output [31:0] s2_Value,
  output [31:0] ra_Value,
  output [31:0] sp_Value,
  output [31:0] Read_Data_1,
  output [31:0] Read_Data_2
);

  wire Register_0_on_off, Register_1_on_off, Register_2_on_off, Register_3_on_off, Register_4_on_off,
       Register_5_on_off, Register_6_on_off, Register_7_on_off, Register_8_on_off, Register_9_on_off,
       Register_10_on_off, Register_11_on_off, Register_12_on_off, Register_13_on_off, Register_14_on_off,
       Register_15_on_off, Register_16_on_off, Register_17_on_off, Register_18_on_off, Register_19_on_off,
       Register_20_on_off, Register_21_on_off, Register_22_on_off, Register_23_on_off, Register_24_on_off,
       Register_25_on_off, Register_26_on_off, Register_27_on_off, Register_28_on_off, Register_29_on_off,
       Register_30_on_off, Register_31_on_off;
  wire [31:0] reg0_out, reg1_out, reg2_out, reg3_out, reg4_out, reg5_out, reg6_out, reg7_out, reg8_out,
       reg9_out, reg10_out, reg11_out, reg12_out, reg13_out, reg14_out, reg15_out, reg19_out, reg20_out,
       reg21_out, reg22_out, reg23_out, reg24_out, reg25_out, reg26_out, reg27_out, reg28_out, reg30_out;

  Register #(.width(32)) register_1 (.Q(reg0_out));  // open: D, en, clk, clr
  Register #(.width(32)) register_2 (.D(Write_Data), .en(Register_1_on_off), .Q(reg1_out), .clk(Clock));  // open: clr
  Register #(.width(32)) register_3 (.D(Write_Data), .en(Register_2_on_off), .Q(reg2_out), .clk(Clock));  // open: clr
  Register #(.width(32)) register_4 (.D(Write_Data), .en(Register_3_on_off), .Q(reg3_out), .clk(Clock));  // open: clr
  Register #(.width(32)) register_5 (.D(Write_Data), .en(Register_4_on_off), .Q(reg4_out), .clk(Clock));  // open: clr
  Register #(.width(32)) register_6 (.D(Write_Data), .en(Register_5_on_off), .Q(reg5_out), .clk(Clock));  // open: clr
  Register #(.width(32)) register_7 (.D(Write_Data), .en(Register_6_on_off), .Q(reg6_out), .clk(Clock));  // open: clr
  Register #(.width(32)) register_8 (.D(Write_Data), .en(Register_7_on_off), .Q(reg7_out), .clk(Clock));  // open: clr
  Register #(.width(32)) register_9 (.D(Write_Data), .en(Register_8_on_off), .Q(reg8_out), .clk(Clock));  // open: clr
  Register #(.width(32)) register_10 (.D(Write_Data), .en(Register_9_on_off), .Q(reg9_out), .clk(Clock));  // open: clr
  Register #(.width(32)) register_11 (
    .D(Write_Data), .en(Register_10_on_off), .Q(reg10_out), .clk(Clock));  // open: clr
  Register #(.width(32)) register_12 (
    .D(Write_Data), .en(Register_11_on_off), .Q(reg11_out), .clk(Clock));  // open: clr
  Register #(.width(32)) register_13 (
    .D(Write_Data), .en(Register_12_on_off), .Q(reg12_out), .clk(Clock));  // open: clr
  Register #(.width(32)) register_14 (
    .D(Write_Data), .en(Register_13_on_off), .Q(reg13_out), .clk(Clock));  // open: clr
  Register #(.width(32)) register_15 (
    .D(Write_Data), .en(Register_14_on_off), .Q(reg14_out), .clk(Clock));  // open: clr
  Register #(.width(32)) register_16 (
    .D(Write_Data), .en(Register_15_on_off), .Q(reg15_out), .clk(Clock));  // open: clr
  Register #(.width(32)) register_17 (.D(Write_Data), .en(Register_16_on_off), .Q(s0_Value), .clk(Clock));  // open: clr
  Register #(.width(32)) register_18 (.D(Write_Data), .en(Register_17_on_off), .Q(s1_Value), .clk(Clock));  // open: clr
  Register #(.width(32)) register_19 (.D(Write_Data), .en(Register_18_on_off), .Q(s2_Value), .clk(Clock));  // open: clr
  Register #(.width(32)) register_20 (
    .D(Write_Data), .en(Register_19_on_off), .Q(reg19_out), .clk(Clock));  // open: clr
  Register #(.width(32)) register_21 (
    .D(Write_Data), .en(Register_20_on_off), .Q(reg20_out), .clk(Clock));  // open: clr
  Register #(.width(32)) register_22 (
    .D(Write_Data), .en(Register_21_on_off), .Q(reg21_out), .clk(Clock));  // open: clr
  Register #(.width(32)) register_23 (
    .D(Write_Data), .en(Register_22_on_off), .Q(reg22_out), .clk(Clock));  // open: clr
  Register #(.width(32)) register_24 (
    .D(Write_Data), .en(Register_23_on_off), .Q(reg23_out), .clk(Clock));  // open: clr
  Register #(.width(32)) register_25 (
    .D(Write_Data), .en(Register_24_on_off), .Q(reg24_out), .clk(Clock));  // open: clr
  Register #(.width(32)) register_26 (
    .D(Write_Data), .en(Register_25_on_off), .Q(reg25_out), .clk(Clock));  // open: clr
  Register #(.width(32)) register_27 (
    .D(Write_Data), .en(Register_26_on_off), .Q(reg26_out), .clk(Clock));  // open: clr
  Register #(.width(32)) register_28 (
    .D(Write_Data), .en(Register_27_on_off), .Q(reg27_out), .clk(Clock));  // open: clr
  Register #(.width(32)) register_29 (
    .D(Write_Data), .en(Register_28_on_off), .Q(reg28_out), .clk(Clock));  // open: clr
  Register #(.width(32)) register_30 (.D(Write_Data), .en(Register_29_on_off), .Q(sp_Value), .clk(Clock));  // open: clr
  Register #(.width(32)) register_31 (
    .D(Write_Data), .en(Register_30_on_off), .Q(reg30_out), .clk(Clock));  // open: clr
  Register #(.width(32)) register_32 (.D(Write_Data), .en(Register_31_on_off), .Q(ra_Value), .clk(Clock));  // open: clr
  Demultiplexer #(.select(5)) demultiplexer_1 (
    .out0(Register_0_on_off), .out1(Register_1_on_off), .out2(Register_2_on_off), .out3(Register_3_on_off),
    .out4(Register_4_on_off), .out5(Register_5_on_off), .out6(Register_6_on_off), .out7(Register_7_on_off),
    .out8(Register_8_on_off), .out9(Register_9_on_off), .out10(Register_10_on_off),
    .out11(Register_11_on_off), .out12(Register_12_on_off), .out13(Register_13_on_off),
    .out14(Register_14_on_off), .out15(Register_15_on_off), .out16(Register_16_on_off),
    .out17(Register_17_on_off), .out18(Register_18_on_off), .out19(Register_19_on_off),
    .out20(Register_20_on_off), .out21(Register_21_on_off), .out22(Register_22_on_off),
    .out23(Register_23_on_off), .out24(Register_24_on_off), .out25(Register_25_on_off),
    .out26(Register_26_on_off), .out27(Register_27_on_off), .out28(Register_28_on_off),
    .out29(Register_29_on_off), .out30(Register_30_on_off), .out31(Register_31_on_off), .in(Write_Enable),
    .sel(Write_Register));  // open: en
  Multiplexer #(.select(5), .width(32)) multiplexer_1 (
    .in0(reg0_out), .in1(reg1_out), .in2(reg2_out), .in3(reg3_out), .in4(reg4_out), .in5(reg5_out),
    .in6(reg6_out), .in7(reg7_out), .in8(reg8_out), .in9(reg9_out), .in10(reg10_out), .in11(reg11_out),
    .in12(reg12_out), .in13(reg13_out), .in14(reg14_out), .in15(reg15_out), .in16(s0_Value), .in17(s1_Value),
    .in18(s2_Value), .in19(reg19_out), .in20(reg20_out), .in21(reg21_out), .in22(reg22_out),
    .in23(reg23_out), .in24(reg24_out), .in25(reg25_out), .in26(reg26_out), .in27(reg27_out),
    .in28(reg28_out), .in29(sp_Value), .in30(reg30_out), .in31(ra_Value), .out(Read_Data_1),
    .sel(Read_Register_1));  // open: en
  Multiplexer #(.select(5), .width(32)) multiplexer_2 (
    .in0(reg0_out), .in1(reg1_out), .in2(reg2_out), .in3(reg3_out), .in4(reg4_out), .in5(reg5_out),
    .in6(reg6_out), .in7(reg7_out), .in8(reg8_out), .in9(reg9_out), .in10(reg10_out), .in11(reg11_out),
    .in12(reg12_out), .in13(reg13_out), .in14(reg14_out), .in15(reg15_out), .in16(s0_Value), .in17(s1_Value),
    .in18(s2_Value), .in19(reg19_out), .in20(reg20_out), .in21(reg21_out), .in22(reg22_out),
    .in23(reg23_out), .in24(reg24_out), .in25(reg25_out), .in26(reg26_out), .in27(reg27_out),
    .in28(reg28_out), .in29(sp_Value), .in30(reg30_out), .in31(ra_Value), .out(Read_Data_2),
    .sel(Read_Register_2));  // open: en

  // Other names for the same wires on the sheet: clk = Clock; read_data1[31:0] = Read_Data_1;
  //   read_data2[31:0] = Read_Data_2; read_reg1[4:0] = Read_Register_1; read_reg2[4:0] = Read_Register_2;
  //   reg16_out[31:0] = s0_Value; reg17_out[31:0] = s1_Value; reg18_out[31:0] = s2_Value; reg29_out[31:0] = sp_Value;
  //   reg31_out[31:0] = ra_Value; write_en = Write_Enable; write_reg[4:0] = Write_Register

  // Notes on the sheet:
  //   INPUTS to your circuit
  //   DON'T CHANGE THE LOCATIONS OF THE INPUTS AND OUTPUTS!
  //   These are DEBUG/TEST outputs from your circuit.
  //   OUTPUTS from your circuit
endmodule
